# Fritzing sketch ledstrip-ethernet-protoboard (saved by Fritzing 0.9.9b)
perfboards: 1

parts:
  Teensy_3_1 = Teensy 3.1
  J1 = HR961160C_1
  J2 = Camdenboss CTB0158-3 [part_number=CTB0158-3 package=THT]
  J3 = Camdenboss CTB0158-3 [part_number=CTB0158-3 package=THT]
  J4 = Camdenboss CTB0158-3 [part_number=CTB0158-3 package=THT]
  J5 = Camdenboss CTB0158-2 [part_number=CTB0158-2 package=THT]
  R4 = Resistor [tolerance=±5% power=0.25 resistance=470 package=THT]
  R5 = Resistor [tolerance=±5% power=0.25 resistance=470 package=THT]
  R6 = Resistor [tolerance=±5% power=0.25 resistance=470 package=THT]
  C4 = Electrolytic Capacitor [capacitance=1000μF voltage=35V package="1010 [SMD, electrolytic]"]
  C5 = Electrolytic Capacitor [capacitance=1000μF voltage=35V package="1010 [SMD, electrolytic]"]
  C6 = Electrolytic Capacitor [capacitance=1000μF voltage=35V package="1010 [SMD, electrolytic]"]

nets:
  N1: Teensy_3_1.D1, R6.Pin_0
  N2: Teensy_3_1.D2, R5.Pin_0
  N3: Teensy_3_1.D3, R4.Pin_0
  N4: Teensy_3_1.D9, J1.connector7
  N5: Teensy_3_1.D10, J1.connector4
  N6: Teensy_3_1.D11, J1.connector2
  N7: Teensy_3_1.D12, J1.connector6
  N8: Teensy_3_1.D13, J1.connector3
  N9: Teensy_3_1.AGND, J2.pin3, J3.pin3, J4.pin3, J5.pin2, C4.-, C5.-, C6.-
  N10: Teensy_3_1.Vin, J1.connector10, J2.pin1, J3.pin1, J4.pin1, J5.pin1, C4.+, C5.+, C6.+
  N11: J2.pin2, R5.Pin_1
  N12: J3.pin2, R4.Pin_1
  N13: J4.pin2, R6.Pin_1
